// Logisim project adder_subtractor_4bit.circ as structural Verilog: 1 circuit, main circuit main
module main (
  input  SUB,
  input  A0,
  input  B0,
  input  A1,
  input  B1,
  input  A2,
  input  B2,
  input  A3,
  input  B3,
  output S0,
  output S1,
  output S2,
  output S3,
  output Cout,
  output V
);

  wire and_1_out, and_2_out, and_3_out, and_4_out, and_5_out, and_6_out, and_7_out, and_8_out, xor_1_p3,
       xor_2_p3, xor_3_p3, xor_4_p3, xor_5_p3, xor_6_p3, xor_7_p3, xor_8_p3, xor_10_p2, xor_11_p2, xor_12_p2;

  // XOR_Gate xor_1: pin names not known; wires that end beside it: B0, SUB, xor_1_p3
  // XOR_Gate xor_2: pin names not known; wires that end beside it: B1, SUB, xor_2_p3
  // XOR_Gate xor_3: pin names not known; wires that end beside it: B2, SUB, xor_3_p3
  // XOR_Gate xor_4: pin names not known; wires that end beside it: B3, SUB, xor_4_p3
  // XOR_Gate xor_5: pin names not known; wires that end beside it: A0, xor_1_p3, xor_5_p3
  and and_1 (and_1_out, A0, xor_1_p3);
  // XOR_Gate xor_6: pin names not known; wires that end beside it: A1, xor_2_p3, xor_6_p3
  and and_2 (and_2_out, A1, xor_2_p3);
  // XOR_Gate xor_7: pin names not known; wires that end beside it: A2, xor_3_p3, xor_7_p3
  and and_3 (and_3_out, A2, xor_3_p3);
  // XOR_Gate xor_8: pin names not known; wires that end beside it: A3, xor_4_p3, xor_8_p3
  and and_4 (and_4_out, A3, xor_4_p3);
  // XOR_Gate xor_9: pin names not known; wires that end beside it: xor_5_p3, SUB, S0
  and and_5 (and_5_out, xor_5_p3, SUB);
  // XOR_Gate xor_10: pin names not known; wires that end beside it: xor_6_p3, xor_10_p2, S1
  and and_6 (and_6_out, xor_6_p3, xor_10_p2);
  // XOR_Gate xor_11: pin names not known; wires that end beside it: xor_7_p3, xor_11_p2, S2
  and and_7 (and_7_out, xor_7_p3, xor_11_p2);
  // XOR_Gate xor_12: pin names not known; wires that end beside it: xor_8_p3, xor_12_p2, S3
  and and_8 (and_8_out, xor_8_p3, xor_12_p2);
  or or_1 (xor_10_p2, and_1_out, and_5_out);
  or or_2 (xor_11_p2, and_2_out, and_6_out);
  or or_3 (xor_12_p2, and_3_out, and_7_out);
  or or_4 (Cout, and_4_out, and_8_out);
  // XOR_Gate xor_13: pin names not known; wires that end beside it: xor_12_p2, Cout, V

  // Notes on the sheet:
  //   4-bit Adder / Subtractor  (SUB=0: S=A+B, SUB=1: S=A-B)
  //   B is XORed with SUB; SUB is also the carry-in (two's complement)
  //   V = signed overflow
endmodule
